// Logisim project miniCurso.circ as structural Verilog: 5 circuits, main circuit main
module main (
  input  A,
  input  B,
  input  carry_in,
  input  in_4,
  input  in_5,
  input  in_6,
  input  A_2,
  input  B_2,
  output carry_out,
  output Soma_Final,
  output carry_out_2,
  output Soma_Final_2,
  output Cin,
  output SomaAB
);

  wire halfadder_1_carry_in, halfadder_1_somaab, halfadder_2_carry_in;

  FullAdder fulladder_1 (
    .B(in_4), .B_2(in_5), .carry_in(in_6), .carry_out_final(carry_out_2), .S(Soma_Final_2));  // open: A, A_2, carry_in_2, Soma_Final, carry_out
  HalfAdder halfadder_1 (.A(A), .B(B), .carry_in(halfadder_1_carry_in), .SomaAB(halfadder_1_somaab));
  FullAdder fulladder_2 ();  // open: A, A_2, B, B_2, carry_in, carry_in_2, Soma_Final, carry_out, carry_out_final, S
  HalfAdder halfadder_2 (.A(halfadder_1_somaab), .B(carry_in), .carry_in(halfadder_2_carry_in), .SomaAB(Soma_Final));
  or or_1 (carry_out, halfadder_1_carry_in, halfadder_2_carry_in);
  and and_1 (Cin, A_2, B_2);
  xor xor_1 (SomaAB, A_2, B_2);
endmodule

module HalfAdder (
  input  A,
  input  B,
  output carry_in,
  output SomaAB
);

  and and_1 (carry_in, A, B);
  xor xor_1 (SomaAB, A, B);
endmodule

module FullAdder (
  input  A,
  input  B,
  input  carry_in,
  input  A_2,
  input  B_2,
  input  carry_in_2,
  output carry_out_final,
  output S,
  output carry_out,
  output Soma_Final
);

  wire and_1_out, and_2_out, halfadder_1_carry_in, halfadder_1_somaab, halfadder_2_carry_in, xor_1_out;

  HalfAdder halfadder_1 (.A(A_2), .B(B_2), .carry_in(halfadder_1_carry_in), .SomaAB(halfadder_1_somaab));
  and and_1 (and_1_out, A, B);
  xor xor_1 (xor_1_out, A, B);
  HalfAdder halfadder_2 (.A(halfadder_1_somaab), .B(carry_in_2), .carry_in(halfadder_2_carry_in), .SomaAB(Soma_Final));
  or or_1 (carry_out, halfadder_1_carry_in, halfadder_2_carry_in);
  xor xor_2 (S, xor_1_out, carry_in);
  and and_2 (and_2_out, xor_1_out, carry_in);
  or or_2 (carry_out_final, and_1_out, and_2_out);

  // Notes on the sheet:
  //   carry out1
  //   S1
  //                     carry out2
endmodule

module RippleCarryAdder (
  input  [7:0] A,
  input  in_2,
  input  [7:0] B,
  input  in_4,
  input  in_5,
  input  in_6,
  input  in_7,
  input  in_8,
  input  in_9,
  input  in_10,
  input  in_11,
  input  in_12,
  input  in_13,
  input  in_14,
  input  in_15,
  input  in_16,
  input  in_17,
  input  in_18,
  input  in_19,
  input  in_20,
  output out_21,
  output [7:0] Resultado_Soma,
  output out_23,
  output out_24,
  output out_25,
  output out_26,
  output out_27,
  output out_28,
  output out_29,
  output out_30,
  output out_31
);

  wire fulladder_2_carry_out_final, fulladder_3_carry_out_final, fulladder_4_carry_out_final,
       fulladder_5_carry_out_final, fulladder_6_carry_out_final, fulladder_7_carry_out_final,
       fulladder_8_carry_out_final, fulladder_9_carry_out_final, fulladder_10_carry_out_final,
       fulladder_11_carry_out_final, fulladder_12_carry_out_final, fulladder_13_carry_out_final,
       fulladder_14_carry_out_final, fulladder_15_carry_out_final;

  FullAdder fulladder_1 (
    .B(A[7]), .B_2(B[7]), .carry_in(fulladder_3_carry_out_final), .carry_out_final(out_21),
    .S(Resultado_Soma[7]));  // open: A, A_2, carry_in_2, Soma_Final, carry_out
  FullAdder fulladder_2 (
    .B(in_5), .B_2(in_6), .carry_in(in_4), .carry_out_final(fulladder_2_carry_out_final), .S(out_23));  // open: A, A_2, carry_in_2, Soma_Final, carry_out
  FullAdder fulladder_3 (
    .B(A[6]), .B_2(B[6]), .carry_in(fulladder_6_carry_out_final),
    .carry_out_final(fulladder_3_carry_out_final), .S(Resultado_Soma[6]));  // open: A, A_2, carry_in_2, Soma_Final, carry_out
  FullAdder fulladder_4 (
    .B(in_7), .B_2(in_8), .carry_in(fulladder_2_carry_out_final),
    .carry_out_final(fulladder_4_carry_out_final), .S(out_24));  // open: A, A_2, carry_in_2, Soma_Final, carry_out
  FullAdder fulladder_5 (
    .B(A[4]), .B_2(B[4]), .carry_in(fulladder_8_carry_out_final),
    .carry_out_final(fulladder_5_carry_out_final), .S(Resultado_Soma[4]));  // open: A, A_2, carry_in_2, Soma_Final, carry_out
  FullAdder fulladder_6 (
    .B(A[5]), .B_2(B[5]), .carry_in(fulladder_5_carry_out_final),
    .carry_out_final(fulladder_6_carry_out_final), .S(Resultado_Soma[5]));  // open: A, A_2, carry_in_2, Soma_Final, carry_out
  FullAdder fulladder_7 (
    .B(in_9), .B_2(in_10), .carry_in(fulladder_4_carry_out_final),
    .carry_out_final(fulladder_7_carry_out_final), .S(out_25));  // open: A, A_2, carry_in_2, Soma_Final, carry_out
  FullAdder fulladder_8 (
    .B(A[3]), .B_2(B[3]), .carry_in(fulladder_10_carry_out_final),
    .carry_out_final(fulladder_8_carry_out_final), .S(Resultado_Soma[3]));  // open: A, A_2, carry_in_2, Soma_Final, carry_out
  FullAdder fulladder_9 (
    .B(in_11), .B_2(in_12), .carry_in(fulladder_7_carry_out_final),
    .carry_out_final(fulladder_9_carry_out_final), .S(out_26));  // open: A, A_2, carry_in_2, Soma_Final, carry_out
  FullAdder fulladder_10 (
    .B(A[2]), .B_2(B[2]), .carry_in(fulladder_12_carry_out_final),
    .carry_out_final(fulladder_10_carry_out_final), .S(Resultado_Soma[2]));  // open: A, A_2, carry_in_2, Soma_Final, carry_out
  FullAdder fulladder_11 (
    .B(in_13), .B_2(in_14), .carry_in(fulladder_9_carry_out_final),
    .carry_out_final(fulladder_11_carry_out_final), .S(out_27));  // open: A, A_2, carry_in_2, Soma_Final, carry_out
  FullAdder fulladder_12 (
    .B(A[1]), .B_2(B[1]), .carry_in(fulladder_14_carry_out_final),
    .carry_out_final(fulladder_12_carry_out_final), .S(Resultado_Soma[1]));  // open: A, A_2, carry_in_2, Soma_Final, carry_out
  FullAdder fulladder_13 (
    .B(in_15), .B_2(in_16), .carry_in(fulladder_11_carry_out_final),
    .carry_out_final(fulladder_13_carry_out_final), .S(out_28));  // open: A, A_2, carry_in_2, Soma_Final, carry_out
  FullAdder fulladder_14 (
    .A(A[1]), .B(A[0]), .B_2(B[0]), .carry_in(in_2), .carry_out_final(fulladder_14_carry_out_final),
    .S(Resultado_Soma[0]));  // open: A_2, carry_in_2, Soma_Final, carry_out
  FullAdder fulladder_15 (
    .B(in_17), .B_2(in_18), .carry_in(fulladder_13_carry_out_final),
    .carry_out_final(fulladder_15_carry_out_final), .S(out_29));  // open: A, A_2, carry_in_2, Soma_Final, carry_out
  FullAdder fulladder_16 (
    .B(in_19), .B_2(in_20), .carry_in(fulladder_15_carry_out_final), .carry_out_final(out_31), .S(out_30));  // open: A, A_2, carry_in_2, Soma_Final, carry_out
endmodule

module FlipFlopRS (
  input  in_1,
  input  in_2,
  input  in_3,
  input  in_4,
  input  in_5,
  input  in_6,
  output out_7,
  output out_8,
  output out_9,
  output out_10,
  output out_11,
  output out_12
);

  wire clock_1_out, or_1_out, or_2_out;

  Clock clock_1 (.out(clock_1_out));
  nand nand_1 (out_7, ~in_1, out_8);  // NAND_Gate
  nand nand_2 (out_8, out_7, ~in_2);  // NAND_Gate
  S_R_Flip_Flop s_r_ff_1 (.S(in_3), .clk(clock_1_out), .R(in_4), .Q(out_9), .Qn(out_10));  // open: preset, reset, en
  or or_1 (or_1_out, in_5, out_12);
  not not_1 (out_11, or_1_out);
  or or_2 (or_2_out, out_11, in_6);
  not not_2 (out_12, or_2_out);
endmodule
